# Fritzing sketch AdfaberArduino2020 (saved by Fritzing 0.9.4)
breadboards: 1

parts:
  R1 = PHOTOCELL [package=photocell]
  OLED1 = OLED 128x64 I2C Monochrome Display
  Part2 = IFR520 MOS module [package=THT]
  S1 = Pushbutton [package="[THT]"]
  M1 = DC Motor
  BAT1 = Battery Holders [package=battery-aa]
  J1 = Piezo Speaker
  S2 = Pushbutton [package="[THT]"]
  S3 = Pushbutton [package="[THT]"]
  WeMos_D1_Mini1 = WeMos D1 Mini

nets:
  N1: R1.P$1, OLED1.GND, Part2.pin3, J1.pin1, WeMos_D1_Mini1.G
  VDD: OLED1.VDD, WeMos_D1_Mini1.5V
  N2: OLED1.SCK, WeMos_D1_Mini1.D2
  N3: OLED1.SDA, WeMos_D1_Mini1.D1
  N4: Part2.pin1, WeMos_D1_Mini1.D8
  N5: Part2.pin4, M1.pin_1
  N6: Part2.pin5, M1.pin_2
  N7: Part2.pin6, BAT1.+
  N8: Part2.pin7, BAT1.-
  N9: S1.Pin_1, S1.Pin_2
  N10: S1.Pin_3, S1.Pin_4
  N11: J1.pin2, WeMos_D1_Mini1.D4
  N12: S2.Pin_1, S2.Pin_2
  N13: S2.Pin_3, S2.Pin_4
  N14: S3.Pin_1, S3.Pin_2
  N15: S3.Pin_3, S3.Pin_4
